# Fritzing sketch fullConnectionDiagram (saved by Fritzing 0.9.4)

parts:
  Part2 = Adafruit BMP388 - Barometric Pressure and Altimeter [part_number="Adafruit #3966"]
  Part3 = Adafruit MicroSD card breakout board [part_number="Adafruit #254"]
  LSM6DSOX1 = Adafruit_LSM6DSOX
  Part1 = Arduino Nano (Rev3.0) (ICSP)
  LPA2 = TSL1401CCS [package="DIP (Dual Inline) [THT]"]
  LPA1 = TSL1401CCS [package="DIP (Dual Inline) [THT]"]
  LPA3 = TSL1401CCS [package="DIP (Dual Inline) [THT]"]
  LPA4 = TSL1401CCS [package="DIP (Dual Inline) [THT]"]
  Part4 = Arduino Mega ADK (Rev3)

nets:
  VDD: Part2.VIN, Part3.VCC, LSM6DSOX1.VCC, Part1.5V, LPA2.VDD, LPA1.VDD, LPA3.VDD, LPA4.VDD
  GND: Part2.GND, Part3.GND, LSM6DSOX1.GND, Part1.GND, LPA2.GND, LPA1.GND, LPA3.GND, LPA4.GND
  N1: Part2.SCK/SCL, Part3.CLK, LSM6DSOX1.SCL, Part1.D13/SCK
  N2: Part2.SDO/ADR, Part3.DO, LSM6DSOX1.SDO, Part1.D12/MISO
  N3: Part2.SDI/SDA, Part3.DI, LSM6DSOX1.SDA, Part1.D11/MOSI
  N4: Part2.CS, Part1.D4
  N5: Part3.CS, Part1.D6
  N6: LSM6DSOX1.CS_5V, Part1.D5
  N7: Part1.D2, LPA2.SI, LPA1.HOLD, LPA1.SI, LPA3.SI, LPA4.SI
  N8: Part1.D3, Part4.D19/RX1
  N9: Part1.A0, LPA2.AO, LPA1.AO, LPA3.AO, LPA4.AO
  N10: LPA2.HOLD, LPA1.SO
  N11: LPA2.SO, LPA4.HOLD
  N12: LPA2.CLK, LPA1.CLK, LPA3.CLK, LPA4.CLK
  N13: LPA3.HOLD, LPA4.SO

notes:
  PDC OUT = GREEN
  PDC IN = ORANGE
  CLOCK = WHITE
  5V = RED
  GND = BLACK

custom parts:
  Adafruit MicroSD card breakout board: Not just a simple breakout board, this microSD adapter goes the extra mile - designed for ease of use. Onboard 5v->3v regulator provides 150mA for power-hungry cards 3v level shifting means you can use this with ease on either 3v or 5v systems Uses a proper level shifting chip, not resistors: less problems, and faster read/write access Use 3 or 4 digital pins to read and write 2Gb+ of storage!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
  TSL1401CCS: The TSL1401CCS Linear Photodiode Array
